# Fritzing sketch circuit (saved by Fritzing 0.9.3b)

parts:
  Part1 = Arduino Nano (Rev3.0)
  J1 = Basic Servo  # not connected
  Part2 = Bluetooth HC-05 Macho

nets:
  N1: Part1.D1/TX, Part2.RXD
  N2: Part1.D0/RX, Part2.TXD
  GND: Part1.GND, Part2.GND
  5V: Part1.5V, Part2.VCC

notes:
  5v 1A
